// Logisim project legacy-logisim-2.7.1.circ as structural Verilog: 1 circuit, main circuit Кибернетика1
module \Кибернетика1  (
  input  x0,
  input  x1,
  output F
);

  wire not_1_p3, not_2_p3;

  // NOT_Gate not_1: pin names not known; wires that end beside it: x0, x1, not_1_p3
  // NOT_Gate not_2: pin names not known; wires that end beside it: x0, x1, not_2_p3
  and and_1 (F, not_1_p3, not_2_p3);
endmodule
